# Fritzing sketch aero-strobe-schema (saved by Fritzing 0.9.3b)

parts:
  12V_Battery = 12 battery [package=battery]
  Arduino_Nano_Every = Arduino Nano (Rev3.0) (ICSP)
  Mosfet_Navigation_Light = IFR520 MOS module [package=THT]
  Mosfet_Wingtip_Strobe_Light = IFR520 MOS module [package=THT]
  LED1 = LED - 3W Aluminum PCB
  LED2 = LED - 3W Aluminum PCB
  LED3 = LED - 3W Aluminum PCB
  LED4 = LED - 3W Aluminum PCB
  LED6 = LED - 3W Aluminum PCB
  LED5 = LED - 3W Aluminum PCB
  LED8 = LED - 3W Aluminum PCB
  LED9 = LED - 3W Aluminum PCB
  Mosfet_Tail_Strobe_Light = IFR520 MOS module [package=THT]
  LED13 = LED - 3W Aluminum PCB
  LED14 = LED - 3W Aluminum PCB
  LED15 = LED - 3W Aluminum PCB
  LED7 = LED - 3W Aluminum PCB
  LED10 = LED - 3W Aluminum PCB
  LED11 = LED - 3W Aluminum PCB
  LED12 = LED - 3W Aluminum PCB

nets:
  GND: 12V_Battery.-, Arduino_Nano_Every.GND, Mosfet_Navigation_Light.GND, Mosfet_Wingtip_Strobe_Light.GND, Mosfet_Tail_Strobe_Light.GND
  VIN: 12V_Battery.+, Arduino_Nano_Every.VIN, Mosfet_Navigation_Light.VIN, Mosfet_Wingtip_Strobe_Light.VIN, Mosfet_Tail_Strobe_Light.VIN
  N1: Arduino_Nano_Every.D6, Mosfet_Tail_Strobe_Light.SIG
  N2: Arduino_Nano_Every.D9, Mosfet_Wingtip_Strobe_Light.SIG
  N3: Arduino_Nano_Every.D10, Mosfet_Navigation_Light.SIG
  N4: Mosfet_Navigation_Light.V+, LED1.anode, LED4.anode
  N5: Mosfet_Navigation_Light.V-, LED3.cathode, LED6.cathode
  N6: Mosfet_Wingtip_Strobe_Light.V+, LED13.anode, LED10.anode
  N7: Mosfet_Wingtip_Strobe_Light.V-, LED15.cathode, LED12.cathode
  N8: LED1.cathode, LED2.anode
  N9: LED2.cathode, LED3.anode
  N10: LED4.cathode, LED5.anode
  N11: LED6.anode, LED5.cathode
  N12: LED8.anode, LED7.cathode
  N13: LED8.cathode, LED9.anode
  N14: LED9.cathode, Mosfet_Tail_Strobe_Light.V-
  N15: Mosfet_Tail_Strobe_Light.V+, LED7.anode
  N16: LED13.cathode, LED14.anode
  N17: LED14.cathode, LED15.anode
  N18: LED10.cathode, LED11.anode
  N19: LED11.cathode, LED12.anode

notes:
  Strobo
  Navigation

custom parts:
  12 battery: 12V lead acid type battery, like the Husqvarna YTH2448 12V 35AH battery. This is the mini version 1/4 the size of the actual battery to be closer to typical breadboard parts (around 2in wide rathher than 7in). The pads in pcb are sized to accomidate up to 14ga wire (as these batterys will deliver high currents.)
  LED - 3W Aluminum PCB: Description: So much power and light from such a small package. This 5 pack of red 3 Watt aluminum backed PCBs is sure to shed a lot of light on any project you add it to. These LEDs act as any other LED except these little guys require much more power while delivering a light as intense of a thousand suns going super nova (this is an exaggeration but you know what we mean)! Each LED in the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
